# Fritzing sketch Fritzing Diagram_Pro_Micro_Motor_Bluetooth_Test (saved by Fritzing 0.9.2b)
breadboards: 1

parts:
  Part1 = Motor Driver 1A Dual TB6612FNG
  Pro_Micro1 = Pro Micro
  M1 = DC Motor
  VCC1 = Battery
  Part2 = Bluetooth HC-06

nets:
  N1: Part1.A02, M1.pin_1
  N2: Part1.A01, M1.pin_2
  GND: Part1.GND, Pro_Micro1.GND, VCC1.-, Part2.GND
  N3: Part1.VM, VCC1.+
  N4: Part1.PWMA, Pro_Micro1.D9
  N5: Part1.AIN2, Pro_Micro1.D10
  N6: Part1.AIN1, Pro_Micro1.D5
  N7: Pro_Micro1.TX1, Part2.RXD
  N8: Pro_Micro1.RX0, Part2.TXD

notes:
  PF7 = Pin A0 = STBY
  PC6 = Pin 5 = AIN1
  PB6 = Pin 10 = AIN2
  PB5 = Pin 9 = PWMA
  PF6 = Pin A1 = BIN1
  PF5 = Pin A2 = BIN2
  PD7 = Pin 6 = PWMB

custom parts:
  Pro Micro: The SparkFun Pro Micro is a complete USB-based microcontoller development system, in a very small footprint, capable of implementing many types of projects. All programming can be done via the USB port.
